// Logisim project CPU.circ as structural Verilog: 8 circuits, main circuit main
// R0
module main (
  output [31:0] out_1,
  output [31:0] out_2,
  output [31:0] out_3,
  output [31:0] out_4,
  output [31:0] out_5,
  output [31:0] out_6,
  output [31:0] out_7,
  output [31:0] out_8
);

  wire _0, _0_t, _0_t_t, alu_1_of, and_1_out, BEQZ, BEQZn, BGEZ, BGEZn, BGTZ, BGTZn, BLEZ, BLEZn, BLTZ,
       BLTZn, BNEZ, BNEZn, clk, EX_MemRd, EX_MemWr, EX_RegWr, ExtOp, Jump_t, JumpR_t, JumpRN, Kill1, Kill2,
       MEM_RegWr, MemRd, MemRdN, MemWr, MemWrN, not_1_out, not_2_out, or_1_out, RegWr, RegWrN, Stall;
  wire [1:0] ALUSrc, ALUSrcN, EX_WBdata, ForwardA, ForwardB, funct, PCSrc, RegDst, WBdata, WBdataN;
  wire [2:0] d, d2, d3, d4, multiplexer_4_out, s, s2, t;
  wire [3:0] ALUop, ALUopN;
  wire [4:0] instructionsplit_1_imm5, opcode;
  wire [7:0] instructionsplit_1_imm8;
  wire [10:0] instructionsplit_1_imm11;
  wire [15:0] instruction, multiplexer_2_out, rom_1_data;
  wire [17:0] multiplexer_9_out;
  wire [19:0] adder_2_out, adder_4_out, bit_extender_1_out, BRANCH, imm8_20bit, imm11_20bit, JUMP, JUMPR,
       multiplexer_1_out, NPC_2_q, NPC_3_q, NPC_q, PC, PC_1;
  wire [31:0] A, ALU_Result, B, bit_extender_2_out, D_q, FW1, FW2, FW3, imm5, imm5_q, imm8, imm11, imm11_q,
       multiplexer_5_out, multiplexer_6_out, multiplexer_8_out, ram_1_data, regfile_1_read_data_1,
       regfile_1_read_data_2, Rs;

  // Probe on out_1
  Bit_Extender #(.in_width(32), .out_width(20), .\type ("sign")) bit_extender_1 (.in(Rs), .out(bit_extender_1_out));
  Register #(.width(20)) NPC (.D(PC), .Q(NPC_q), .clk(clk));  // open: en, clr
  Register #(.width(20)) NPC_2 (.D(PC), .Q(NPC_2_q), .clk(clk));  // open: en, clr
  // Probe on out_2
  Multiplexer #(.select(2), .width(20), .enable("false")) multiplexer_1 (
    .in0(PC_1), .in1(JUMP), .in2(BRANCH), .in3(JUMPR), .out(multiplexer_1_out), .sel(PCSrc));
  not not_1 (not_1_out, Stall);
  Adder #(.width(20)) adder_1 (.a(20'h1), .b(PC), .out(PC_1));  // open: cin, cout
  Register #(.width(20)) NPC_3 (.D(bit_extender_1_out), .Q(NPC_3_q), .clk(clk));  // open: en, clr
  // Probe on out_3
  Register #(.width(20)) currPC (.D(multiplexer_1_out), .en(not_1_out), .Q(PC), .clk(clk));  // open: clr
  Adder #(.width(20)) adder_2 (.a(imm8_20bit), .b(NPC_3_q), .out(adder_2_out));  // open: cin, cout
  Adder #(.width(20)) adder_3 (.a(imm11_20bit), .b(NPC_q), .out(JUMP));  // open: cin, cout
  Adder #(.width(20)) adder_4 (.a(imm8_20bit), .b(NPC_2_q), .out(adder_4_out));  // open: cin, cout
  // Probe on PC
  Register #(.width(20)) BTA (.D(adder_2_out), .Q(JUMPR), .clk(clk));  // open: en, clr
  Register #(.width(20)) BTA_2 (.D(adder_4_out), .Q(BRANCH), .clk(clk));  // open: en, clr
  // Probe on out_4
  Clock CLOCK (.out(clk));
  // Probe on out_5
  ROM #(.addrWidth(20), .dataWidth(16)) rom_1 (.addr(PC), .data(rom_1_data));  // open: sel
  Multiplexer #(.width(16), .enable("false")) multiplexer_2 (
    .in0(rom_1_data), .in1({16{1'b0}}), .out(multiplexer_2_out), .sel(Kill1));
  not not_2 (not_2_out, Stall);
  PCControl pccontrol_1 (
    .JumpR(JumpR_t), .Jump(Jump_t), .BEQZ(BEQZ), ._0(_0_t_t), ._0_2(_0_t), ._0_3(_0), .PCSrc(PCSrc),
    .Kill1(Kill1), .Kill2(Kill2), .BNEZ(BNEZ), .BLTZ(BLTZ), .BGEZ(BGEZ), .BGTZ(BGTZ), .BLEZ(BLEZ));
  // Probe on out_6
  Register #(.width(16)) Inst (.D(multiplexer_2_out), .en(not_2_out), .Q(instruction), .clk(clk));  // open: clr
  // Probe on out_7
  // Probe on out_8
  InstructionSplit instructionsplit_1 (
    .Instruction(instruction), .opcode(opcode), .rs(s), .rt(t), .rd(d), .funct(funct),
    .imm5(instructionsplit_1_imm5), .imm8(instructionsplit_1_imm8), .imm11(instructionsplit_1_imm11));
  Extendor extendor_1 (
    .extOp(ExtOp), .imm5(instructionsplit_1_imm5), .imm8(instructionsplit_1_imm8),
    .imm11(instructionsplit_1_imm11), .OImm5(imm5), .OImm8(imm8), .OImm11(imm11), .OImm11_20bit(imm11_20bit),
    .OImm8_20bit(imm8_20bit));
  and and_1 (and_1_out, RegDst[1], RegDst[0]);
  Multiplexer #(.width(3), .enable("false")) multiplexer_3 (.in0(s), .in1(3'b000), .out(s2), .sel(and_1_out));
  Multiplexer #(.select(2), .width(3), .enable("false")) multiplexer_4 (
    .in0(t), .in1(d), .in2(3'b111), .in3(3'b000), .out(multiplexer_4_out), .sel(RegDst));
  ControlUnit controlunit_1 (
    .opCode(opcode), .func(funct), .RegDst(RegDst), .RegWr(RegWrN), .MemRd(MemRdN), .MemWr(MemWrN),
    .ALUSrc(ALUSrcN), .ExtOp(ExtOp), .WBdata(WBdataN), .ALUop(ALUopN), .Jump(Jump_t), .JumpR(JumpRN),
    .BEQZ(BEQZn), .BNEZ(BNEZn), .BLTZ(BLTZn), .BGEZ(BGEZn), .BGTZ(BGTZn), .BLEZ(BLEZn));
  RegFile regfile_1 (
    .Read_register_A(s2), .Read_register_B(t), .write_register_W(d4), .write_data(FW3), .Clock(clk),
    .Read_Data_1(regfile_1_read_data_1), .Read_Data_2(regfile_1_read_data_2), .Reg_0_Value(out_1),
    .Reg_1_Value(out_2), .Reg_2_Value(out_3), .Reg_3_Value(out_4), .Reg_4_Value(out_5), .Reg_5_Value(out_6),
    .Reg_6_Value(out_7), .Reg_7_Value(out_8), .RegWrite(RegWr));  // open: Clear
  HazardUnit hazardunit_1 (
    .ForwardA(ForwardA), .ForwardB(ForwardB), .Stall(Stall), .s(s2), .t(t), .d2(d2), .d3(d3), .d4(d4),
    .EX_RegWr(EX_RegWr), .MEM_RegWr(MEM_RegWr), .WB_RegWr(RegWr), .EX_MemRd(EX_MemRd));
  Multiplexer #(.select(2), .width(32), .enable("false")) multiplexer_5 (
    .in0(regfile_1_read_data_1), .in1(FW1), .in2(FW2), .in3(FW3), .out(multiplexer_5_out), .sel(ForwardA));
  Multiplexer #(.select(2), .width(32), .enable("false")) multiplexer_6 (
    .in0(regfile_1_read_data_2), .in1(FW1), .in2(FW2), .in3(FW3), .out(multiplexer_6_out), .sel(ForwardB));
  Register #(.width(32)) u_A (.D(multiplexer_5_out), .Q(A), .clk(clk));  // open: en, clr
  Register #(.width(32)) u_B (.D(multiplexer_6_out), .Q(B), .clk(clk));  // open: en, clr
  Register #(.width(3)) u_d2 (.D(multiplexer_4_out), .Q(d2), .clk(clk));  // open: en, clr
  Register #(.width(32)) u_imm5 (.D(imm5), .Q(imm5_q), .clk(clk));  // open: en, clr
  Register #(.width(32)) u_imm11 (.D(imm11), .Q(imm11_q), .clk(clk));  // open: en, clr
  Multiplexer #(.select(2), .width(32), .enable("false")) multiplexer_7 (
    .in0(A), .in1(A), .in2(A), .in3({32{1'b0}}), .out(Rs), .sel(ALUSrc));
  Multiplexer #(.select(2), .width(32), .enable("false")) multiplexer_8 (
    .in0(B), .in1(imm5_q), .in2(imm11_q), .in3(imm11_q), .out(multiplexer_8_out), .sel(ALUSrc));
  or or_1 (or_1_out, Kill2, Stall);
  Multiplexer #(.width(18), .enable("false")) multiplexer_9 (
    .in0({BLEZn, BGTZn, BGEZn, BLTZn, BNEZn, BEQZn, JumpRN, RegWrN, WBdataN, MemWrN, MemRdN, ALUopN, ALUSrcN}),
    .in1({18{1'b0}}), .out(multiplexer_9_out), .sel(or_1_out));
  Register #(.width(18)) EX (
    .D(multiplexer_9_out),
    .Q({BLEZ, BGTZ, BGEZ, BLTZ, BNEZ, BEQZ, JumpR_t, EX_RegWr, EX_WBdata, EX_MemWr, EX_MemRd, ALUop, ALUSrc}),
    .clk(clk));  // open: en, clr
  ALU alu_1 (
    .A(Rs), .B(multiplexer_8_out), .ALUop(ALUop), .Result(FW1), .OF(alu_1_of), .GTZ(_0_t_t), .EQZ(_0_t),
    .LTZ(_0));
  LED led_1 (.in(alu_1_of));
  Register #(.width(32)) R (.D(FW1), .Q(ALU_Result), .clk(clk));  // open: en, clr
  Register #(.width(3)) u_d3 (.D(d2), .Q(d3), .clk(clk));  // open: en, clr
  Register #(.width(32)) u_D (.D(B), .Q(D_q), .clk(clk));  // open: en, clr
  Register #(.width(5)) MEM (
    .D({EX_RegWr, EX_WBdata, EX_MemWr, EX_MemRd}), .Q({MEM_RegWr, WBdata, MemWr, MemRd}), .clk(clk));  // open: en, clr
  RAM #(.addrWidth(20), .dataWidth(32), .bus("separate")) ram_1 (
    .addr(ALU_Result[19:0]), .din(D_q), .data(ram_1_data), .str(MemWr), .clk(clk), .ld(MemRd));  // open: sel, clr
  assign bit_extender_2_out = {{12{PC_1[19]}}, PC_1};  // Bit_Extender bit_extender_2
  Multiplexer #(.select(2), .width(32), .enable("false")) multiplexer_10 (
    .in0(ALU_Result), .in1(ram_1_data), .in2(bit_extender_2_out), .out(FW2), .sel(WBdata));  // open: in3
  Register #(.width(32)) Data (.D(FW2), .Q(FW3), .clk(clk));  // open: en, clr
  Register #(.width(3)) u_d4 (.D(d3), .Q(d4), .clk(clk));  // open: en, clr
  Register #(.width(1)) WB (.D(MEM_RegWr), .Q(RegWr), .clk(clk));  // open: en, clr

  // Other names for the same wires on the sheet: DataIn[31:0] = B; R0[31:0] = out_1; R1[31:0] = out_2;
  //   R2[31:0] = out_3; R3[31:0] = out_4; R4[31:0] = out_5; R5[31:0] = out_6; R6[31:0] = out_7; R7[31:0] = out_8;
  //   WriteData[31:0] = FW3

  // Notes on the sheet:
  //   Next PC
  //   Instruction Fetch
  //   IF = Instruction Fetch
  //   Instruction Memory
  //   PC Control
  //   Instruction Spliter
  //   jalr, jal
  //   set, sset
  //   Control Unit
  //   ID = Instruction Decode
  //   Register File
  //   Hazard Unit
  //   ALU
  //   EX = Execute
  //   Data Memory
  //   MEM = Memory Access
  //   WB = Write Back
endmodule

module InstructionSplit (
  input  [15:0] Instruction,
  output [4:0] opcode,
  output [2:0] rs,
  output [2:0] rt,
  output [2:0] rd,
  output [1:0] funct,
  output [4:0] imm5,
  output [7:0] imm8,
  output [10:0] imm11
);


  assign funct = Instruction[1:0];
  assign imm5 = Instruction[4:0];
  assign imm8 = Instruction[7:0];
  assign imm11 = Instruction[10:0];
  assign opcode = Instruction[15:11];
  assign rd = Instruction[4:2];
  assign rs = Instruction[10:8];
  assign rt = Instruction[7:5];

  // Notes on the sheet:
  //   Instruction Spliter
endmodule

// Ext
module Extendor (
  input  extOp,
  input  [4:0] imm5,
  input  [7:0] imm8,
  input  [10:0] imm11,
  output [31:0] OImm5,
  output [31:0] OImm8,
  output [31:0] OImm11,
  output [19:0] OImm8_20bit,
  output [19:0] OImm11_20bit
);

  wire multiplexer_1_out, multiplexer_2_out, multiplexer_3_out, multiplexer_4_out, multiplexer_5_out;

  Multiplexer #(.enable("false")) multiplexer_1 (.in0(1'b0), .in1(imm5[4]), .out(multiplexer_1_out), .sel(extOp));
  assign OImm5 = {{27{multiplexer_1_out}}, imm5};  // Bit_Extender bit_extender_1
  Multiplexer #(.enable("false")) multiplexer_2 (.in0(1'b0), .in1(imm8[7]), .out(multiplexer_2_out), .sel(extOp));
  assign OImm8 = {{24{multiplexer_2_out}}, imm8};  // Bit_Extender bit_extender_2
  Multiplexer #(.enable("false")) multiplexer_3 (.in0(1'b0), .in1(imm11[10]), .out(multiplexer_3_out), .sel(extOp));
  assign OImm11 = {{21{multiplexer_3_out}}, imm11};  // Bit_Extender bit_extender_3
  Multiplexer #(.enable("false")) multiplexer_4 (.in0(1'b0), .in1(imm8[7]), .out(multiplexer_4_out), .sel(extOp));
  assign OImm8_20bit = {{12{multiplexer_4_out}}, imm8};  // Bit_Extender bit_extender_4
  Multiplexer #(.enable("false")) multiplexer_5 (.in0(1'b0), .in1(imm11[10]), .out(multiplexer_5_out), .sel(extOp));
  assign OImm11_20bit = {{9{multiplexer_5_out}}, imm11};  // Bit_Extender bit_extender_5

  // Notes on the sheet:
  //   EXTENDOR
  //   OUTPUT
  //   INPUT
endmodule

module ControlUnit (
  input  [4:0] opCode,
  input  [1:0] func,
  output [1:0] RegDst,
  output RegWr,
  output MemRd,
  output MemWr,
  output [1:0] ALUSrc,
  output ExtOp,
  output [1:0] WBdata,
  output [3:0] ALUop,
  output Jump,
  output JumpR,
  output BEQZ,
  output BNEZ,
  output BLTZ,
  output BGEZ,
  output BGTZ,
  output BLEZ
);

  wire ADD, ADDI, AND, ANDI, CAND, CANDI, comparator_1_eq, comparator_2_eq, comparator_3_eq, comparator_4_eq,
       comparator_5_eq, comparator_6_eq, comparator_7_eq, comparator_8_eq, comparator_9_eq, comparator_10_eq,
       comparator_11_eq, comparator_12_eq, comparator_13_eq, comparator_14_eq, comparator_15_eq,
       comparator_16_eq, decoder_1_out0, decoder_1_out1, J, JAL, JALR, JR, LW, NADD, NADDI, OR, or_1_out,
       or_2_out, or_3_out, or_4_out, or_6_out, or_7_out, or_8_out, or_9_out, ORI, R_type, ROR, SET, SLL, SLT,
       SLTI, SLTU, SLTUI, SRA, SRL, SSET, SW, XOR, XORI;
  wire [3:0] multiplexer_1_out, multiplexer_2_out, multiplexer_3_out, multiplexer_4_out, multiplexer_5_out,
       multiplexer_6_out, multiplexer_7_out, multiplexer_8_out, multiplexer_9_out, multiplexer_10_out,
       multiplexer_11_out, multiplexer_12_out;

  Decoder #(.select(5), .enable("false")) decoder_1 (
    .out0(decoder_1_out0), .out1(decoder_1_out1), .out4(ANDI), .out5(CANDI), .out6(ORI), .out7(XORI),
    .out8(ADDI), .out9(NADDI), .out10(SLTI), .out11(SLTUI), .out12(SLL), .out13(SRL), .out14(SRA),
    .out15(ROR), .out16(LW), .out17(SW), .out20(BEQZ), .out21(BNEZ), .out22(BLTZ), .out23(BGEZ),
    .out24(BGTZ), .out25(BLEZ), .out26(JR), .out27(JALR), .out28(SET), .out29(SSET), .out30(J), .out31(JAL),
    .sel(opCode));  // open: out2, out3, out18, out19
  Multiplexer #(.width(4), .enable("false")) multiplexer_1 (
    .in0(4'b0000), .in1(4'b0000), .out(multiplexer_1_out), .sel(or_1_out));
  or or_1 (or_1_out, AND, ANDI);
  Multiplexer #(.width(4), .enable("false")) multiplexer_2 (
    .in0(multiplexer_1_out), .in1(4'b0001), .out(multiplexer_2_out), .sel(or_2_out));
  or or_2 (or_2_out, CAND, CANDI);
  Multiplexer #(.width(4), .enable("false")) multiplexer_3 (
    .in0(multiplexer_2_out), .in1(4'b0010), .out(multiplexer_3_out), .sel(or_3_out));
  or or_3 (or_3_out, OR, ORI);
  or or_4 (or_4_out, XOR, XORI);
  Multiplexer #(.width(4), .enable("false")) multiplexer_4 (
    .in0(multiplexer_3_out), .in1(4'b0011), .out(multiplexer_4_out), .sel(or_4_out));
  or or_5 (R_type, decoder_1_out0, decoder_1_out1);
  Multiplexer #(.width(4), .enable("false")) multiplexer_5 (
    .in0(multiplexer_4_out), .in1(4'b0100), .out(multiplexer_5_out), .sel(or_6_out));
  or or_6 (or_6_out, SW, ADD, SET, ADDI, LW);
  Multiplexer #(.width(4), .enable("false")) multiplexer_6 (
    .in0(multiplexer_5_out), .in1(4'b0101), .out(multiplexer_6_out), .sel(or_7_out));
  or or_7 (or_7_out, NADD, NADDI);
  or or_8 (or_8_out, SLT, SLTI);
  Multiplexer #(.width(4), .enable("false")) multiplexer_7 (
    .in0(multiplexer_6_out), .in1(4'b0110), .out(multiplexer_7_out), .sel(or_8_out));
  or or_9 (or_9_out, SLTU, SLTUI);
  or or_10 (Jump, JAL, J);
  Comparator #(.width(2), .mode("unsigned")) comparator_1 (.a(func), .b(2'b00), .eq(comparator_1_eq));  // open: gt, lt
  Comparator #(.width(5), .mode("unsigned")) comparator_2 (
    .a(5'b00001), .b(opCode), .eq(comparator_2_eq));  // open: gt, lt
  Comparator #(.width(2), .mode("unsigned")) comparator_3 (.a(func), .b(2'b01), .eq(comparator_3_eq));  // open: gt, lt
  Comparator #(.width(5), .mode("unsigned")) comparator_4 (
    .a(5'b00001), .b(opCode), .eq(comparator_4_eq));  // open: gt, lt
  Comparator #(.width(2), .mode("unsigned")) comparator_5 (.a(func), .b(2'b00), .eq(comparator_5_eq));  // open: gt, lt
  Comparator #(.width(5), .mode("unsigned")) comparator_6 (
    .a({5{1'b0}}), .b(opCode), .eq(comparator_6_eq));  // open: gt, lt
  Comparator #(.width(2), .mode("unsigned")) comparator_7 (.a(func), .b(2'b01), .eq(comparator_7_eq));  // open: gt, lt
  Comparator #(.width(5), .mode("unsigned")) comparator_8 (
    .a({5{1'b0}}), .b(opCode), .eq(comparator_8_eq));  // open: gt, lt
  Multiplexer #(.width(4), .enable("false")) multiplexer_8 (
    .in0(multiplexer_7_out), .in1(4'b0111), .out(multiplexer_8_out), .sel(or_9_out));
  Multiplexer #(.width(4), .enable("false")) multiplexer_9 (
    .in0(multiplexer_8_out), .in1(4'b1000), .out(multiplexer_9_out), .sel(SLL));
  or or_11 (JumpR, JALR, JR);
  and and_1 (ADD, comparator_1_eq, comparator_2_eq);
  and and_2 (NADD, comparator_3_eq, comparator_4_eq);
  and and_3 (AND, comparator_5_eq, comparator_6_eq);
  and and_4 (CAND, comparator_7_eq, comparator_8_eq);
  Multiplexer #(.width(4), .enable("false")) multiplexer_10 (
    .in0(multiplexer_9_out), .in1(4'b1001), .out(multiplexer_10_out), .sel(SRL));
  ROM #(.addrWidth(5), .dataWidth(10)) rom_1 (
    .addr(opCode), .data({RegDst, RegWr, ExtOp, ALUSrc, MemRd, MemWr, WBdata}));  // open: sel
  // Probe on {RegDst, RegWr, ExtOp, ALUSrc, MemRd, MemWr, WBdata}
  Multiplexer #(.width(4), .enable("false")) multiplexer_11 (
    .in0(multiplexer_10_out), .in1(4'b1010), .out(multiplexer_11_out), .sel(SRA));
  Comparator #(.width(2), .mode("unsigned")) comparator_9 (.a(func), .b(2'b10), .eq(comparator_9_eq));  // open: gt, lt
  Comparator #(.width(5), .mode("unsigned")) comparator_10 (
    .a(5'b00001), .b(opCode), .eq(comparator_10_eq));  // open: gt, lt
  Comparator #(.width(2), .mode("unsigned")) comparator_11 (
    .a(func), .b(2'b11), .eq(comparator_11_eq));  // open: gt, lt
  Comparator #(.width(5), .mode("unsigned")) comparator_12 (
    .a(5'b00001), .b(opCode), .eq(comparator_12_eq));  // open: gt, lt
  Comparator #(.width(2), .mode("unsigned")) comparator_13 (
    .a(func), .b(2'b10), .eq(comparator_13_eq));  // open: gt, lt
  Comparator #(.width(5), .mode("unsigned")) comparator_14 (
    .a({5{1'b0}}), .b(opCode), .eq(comparator_14_eq));  // open: gt, lt
  Comparator #(.width(2), .mode("unsigned")) comparator_15 (
    .a(func), .b(2'b11), .eq(comparator_15_eq));  // open: gt, lt
  Comparator #(.width(5), .mode("unsigned")) comparator_16 (
    .a({5{1'b0}}), .b(opCode), .eq(comparator_16_eq));  // open: gt, lt
  Multiplexer #(.width(4), .enable("false")) multiplexer_12 (
    .in0(multiplexer_11_out), .in1(4'b1011), .out(multiplexer_12_out), .sel(ROR));
  and and_5 (SLT, comparator_9_eq, comparator_10_eq);
  and and_6 (SLTU, comparator_11_eq, comparator_12_eq);
  and and_7 (OR, comparator_13_eq, comparator_14_eq);
  and and_8 (XOR, comparator_15_eq, comparator_16_eq);
  Multiplexer #(.width(4), .enable("false")) multiplexer_13 (
    .in0(multiplexer_12_out), .in1(4'b1100), .out(ALUop), .sel(SSET));

  // Notes on the sheet:
  //   Control Unit:
  //   Main Control
  //   ALU Control
  //   inputs
  //   contents of rom_1 (hex, n*v repeats v):
  //   180 180 0 0 8*d0 4*90 d9 54 0 0 7*40 2c2 3f0 3a0 40 2c2
  //   outputs
endmodule

module RegFile (
  input  [2:0] Read_register_A,
  input  [2:0] Read_register_B,
  input  [2:0] write_register_W,
  input  [31:0] write_data,
  input  RegWrite,
  input  Clear,
  input  Clock,
  output [31:0] Reg_0_Value,
  output [31:0] Reg_1_Value,
  output [31:0] Reg_2_Value,
  output [31:0] Reg_3_Value,
  output [31:0] Reg_4_Value,
  output [31:0] Reg_5_Value,
  output [31:0] Reg_6_Value,
  output [31:0] Reg_7_Value,
  output [31:0] Read_Data_1,
  output [31:0] Read_Data_2
);

  wire WriteReg0, WriteReg1, WriteReg2, WriteReg3, WriteReg4, WriteReg5, WriteReg6, WriteReg7;

  Demultiplexer #(.select(3), .enable("false")) demultiplexer_1 (
    .out0(WriteReg0), .out1(WriteReg1), .out2(WriteReg2), .out3(WriteReg3), .out4(WriteReg4),
    .out5(WriteReg5), .out6(WriteReg6), .out7(WriteReg7), .in(RegWrite), .sel(write_register_W));
  Register #(.width(32)) register_1 (.D(write_data), .en(WriteReg0), .Q(Reg_0_Value), .clk(Clock), .clr(Clear));
  Register #(.width(32)) register_2 (.D(write_data), .en(WriteReg1), .Q(Reg_1_Value), .clk(Clock), .clr(Clear));
  Register #(.width(32)) register_3 (.D(write_data), .en(WriteReg2), .Q(Reg_2_Value), .clk(Clock), .clr(Clear));
  Register #(.width(32)) register_4 (.D(write_data), .en(WriteReg3), .Q(Reg_3_Value), .clk(Clock), .clr(Clear));
  Register #(.width(32)) register_5 (.D(write_data), .en(WriteReg4), .Q(Reg_4_Value), .clk(Clock), .clr(Clear));
  Register #(.width(32)) register_6 (.D(write_data), .en(WriteReg5), .Q(Reg_5_Value), .clk(Clock), .clr(Clear));
  Register #(.width(32)) register_7 (.D(write_data), .en(WriteReg6), .Q(Reg_6_Value), .clk(Clock), .clr(Clear));
  Register #(.width(32)) register_8 (.D(write_data), .en(WriteReg7), .Q(Reg_7_Value), .clk(Clock), .clr(Clear));
  Multiplexer #(.select(3), .width(32), .enable("false")) multiplexer_1 (
    .in0(Reg_0_Value), .in1(Reg_1_Value), .in2(Reg_2_Value), .in3(Reg_3_Value), .in4(Reg_4_Value),
    .in5(Reg_5_Value), .in6(Reg_6_Value), .in7(Reg_7_Value), .out(Read_Data_1), .sel(Read_register_A));
  Multiplexer #(.select(3), .width(32), .enable("false")) multiplexer_2 (
    .in0(Reg_0_Value), .in1(Reg_1_Value), .in2(Reg_2_Value), .in3(Reg_3_Value), .in4(Reg_4_Value),
    .in5(Reg_5_Value), .in6(Reg_6_Value), .in7(Reg_7_Value), .out(Read_Data_2), .sel(Read_register_B));

  // Other names for the same wires on the sheet: CLK = Clock; Data[31:0] = write_data; ReadA[2:0] = Read_register_A;
  //   ReadB[2:0] = Read_register_B; Reg0[31:0] = Reg_0_Value; Reg1[31:0] = Reg_1_Value; Reg2[31:0] = Reg_2_Value;
  //   Reg3[31:0] = Reg_3_Value; Reg4[31:0] = Reg_4_Value; Reg5[31:0] = Reg_5_Value; Reg6[31:0] = Reg_6_Value;
  //   Reg7[31:0] = Reg_7_Value; WriteSel[2:0] = write_register_W

  // Notes on the sheet:
  //   Register File
  //   These are INPUTS to the circuit
  //   These are OUTPUTS to the circuit
  //   Write Part
  //   Read Part
  //   These are OUTPUTS to the circuit
endmodule

module ALU (
  input  [31:0] A,
  input  [31:0] B,
  input  [3:0] ALUop,
  output [31:0] Result,
  output GTZ,
  output OF,
  output EQZ,
  output LTZ
);

  wire and_3_out, and_4_out, comparator_1_lt, comparator_2_lt, NADD, overflow;
  wire [31:0] ADD___NADD, AND, CAND, multiplexer_1_out, negator_1_out, not_1_out, OR, ROR, shifter_1_out,
       SLL, SLT, SLTU, SRA, SRL, SSET, XOR;

  assign not_1_out = ~A;  // NOT_Gate not_1, 32 bits wide
  Negator #(.width(32)) negator_1 (.in(A), .out(negator_1_out));
  assign AND = A & B;  // AND_Gate and_1, 32 bits wide
  assign CAND = not_1_out & B;  // AND_Gate and_2, 32 bits wide
  assign OR = A | B;  // OR_Gate or_1, 32 bits wide
  assign XOR = A ^ B;  // XOR_Gate xor_1, 32 bits wide
  Multiplexer #(.width(32), .enable("false")) multiplexer_1 (
    .in0(A), .in1(negator_1_out), .out(multiplexer_1_out), .sel(NADD));
  and and_3 (and_3_out, ~B[31], ~A[31], ADD___NADD[31], ~NADD);  // AND_Gate
  and and_4 (and_4_out, B[31], A[31], ~ADD___NADD[31], NADD);  // AND_Gate
  Comparator #(.width(32)) comparator_1 (.a(A), .b(B), .lt(comparator_1_lt));  // open: gt, eq
  Comparator #(.width(32), .mode("unsigned")) comparator_2 (.a(A), .b(B), .lt(comparator_2_lt));  // open: gt, eq
  assign SLT = {{31{1'b0}}, comparator_1_lt};  // Bit_Extender bit_extender_1
  assign SLTU = {{31{1'b0}}, comparator_2_lt};  // Bit_Extender bit_extender_2
  Shifter #(.width(32)) shifter_1 (.in(A), .\dist (5'b01011), .out(shifter_1_out));
  Shifter #(.width(32)) shifter_2 (.in(A), .\dist (B[4:0]), .out(SLL));
  Shifter #(.width(32), .shift("lr")) shifter_3 (.in(A), .\dist (B[4:0]), .out(SRL));
  Shifter #(.width(32), .shift("ar")) shifter_4 (.in(A), .\dist (B[4:0]), .out(SRA));
  Shifter #(.width(32), .shift("rr")) shifter_5 (.in(A), .\dist (B[4:0]), .out(ROR));
  Comparator #(.width(32)) comparator_3 (.a(A), .b({32{1'b0}}), .gt(GTZ), .eq(EQZ), .lt(LTZ));
  Adder #(.width(32)) adder_1 (.a(multiplexer_1_out), .b(B), .out(ADD___NADD), .cin(1'b0));  // open: cout
  assign SSET = shifter_1_out | B;  // OR_Gate or_2, 32 bits wide
  or or_3 (overflow, and_3_out, and_4_out);
  Multiplexer #(.select(4), .width(32), .enable("false")) multiplexer_2 (
    .in0(AND), .in1(CAND), .in2(OR), .in3(XOR), .in4(ADD___NADD), .in5(ADD___NADD), .in6(SLT), .in7(SLTU),
    .in8(SLL), .in9(SRL), .in10(SRA), .in11(ROR), .in12(SSET), .out(Result), .sel(ALUop));  // open: in13, in14, in15
  Comparator #(.width(4), .mode("unsigned")) comparator_4 (.a(4'b0101), .b(ALUop), .eq(NADD));  // open: gt, lt
  Multiplexer #(.select(4), .enable("false")) multiplexer_3 (
    .in0(1'b0), .in1(1'b0), .in2(1'b0), .in3(1'b0), .in4(overflow), .in5(overflow), .in6(1'b0), .in7(1'b0),
    .in8(1'b0), .in9(1'b0), .in10(1'b0), .in11(1'b0), .in12(1'b0), .in13(1'b0), .in14(1'b0), .in15(1'b0),
    .out(OF), .sel(ALUop));

  // Other names for the same wires on the sheet: _0 = LTZ; _0_t = EQZ; _0_t_t = GTZ; shiftAmount[4:0] = B[4:0]

  // Notes on the sheet:
  //   ALU
  //   ALU operations:
  //   Shift/Rotate Operation:
  //   Logical Operation:
  //   Arthimatic Operation:
  //   Overflow Detection
  //   Set Less Than ( slt / sltu ) :
  //   input:
  //   ALU Multiplexer:
  //   Branch Flags
endmodule

module HazardUnit (
  input  [2:0] s,
  input  [2:0] t,
  input  [2:0] d2,
  input  [2:0] d3,
  input  [2:0] d4,
  input  EX_RegWr,
  input  MEM_RegWr,
  input  WB_RegWr,
  input  EX_MemRd,
  output [1:0] ForwardA,
  output [1:0] ForwardB,
  output Stall
);

  wire comparator_1_eq, comparator_2_eq, comparator_3_eq, comparator_4_eq, comparator_5_eq, comparator_6_eq,
       EC1A, EC1B, EC2A, EC2B, EC3A, EC3B, or_1_out;
  wire [1:0] multiplexer_1_out, multiplexer_2_out, multiplexer_3_out, multiplexer_4_out;

  Comparator #(.width(3), .mode("unsigned")) comparator_1 (.a(s), .b(d2), .eq(comparator_1_eq));  // open: gt, lt
  Comparator #(.width(3), .mode("unsigned")) comparator_2 (.a(s), .b(d3), .eq(comparator_2_eq));  // open: gt, lt
  Comparator #(.width(3), .mode("unsigned")) comparator_3 (.a(s), .b(d4), .eq(comparator_3_eq));  // open: gt, lt
  Comparator #(.width(3), .mode("unsigned")) comparator_4 (.a(t), .b(d2), .eq(comparator_4_eq));  // open: gt, lt
  Comparator #(.width(3), .mode("unsigned")) comparator_5 (.a(t), .b(d3), .eq(comparator_5_eq));  // open: gt, lt
  Comparator #(.width(3), .mode("unsigned")) comparator_6 (.a(t), .b(d4), .eq(comparator_6_eq));  // open: gt, lt
  and and_1 (EC1A, comparator_1_eq, EX_RegWr);
  and and_2 (EC2A, comparator_2_eq, MEM_RegWr);
  and and_3 (EC3A, comparator_3_eq, WB_RegWr);
  and and_4 (EC1B, comparator_4_eq, EX_RegWr);
  and and_5 (EC2B, comparator_5_eq, MEM_RegWr);
  and and_6 (EC3B, comparator_6_eq, WB_RegWr);
  Multiplexer #(.width(2), .enable("false")) multiplexer_1 (
    .in0(2'b00), .in1(2'b11), .out(multiplexer_1_out), .sel(EC3A));
  Multiplexer #(.width(2), .enable("false")) multiplexer_2 (
    .in0(2'b00), .in1(2'b11), .out(multiplexer_2_out), .sel(EC3B));
  Multiplexer #(.width(2), .enable("false")) multiplexer_3 (
    .in0(multiplexer_1_out), .in1(2'b10), .out(multiplexer_3_out), .sel(EC2A));
  Multiplexer #(.width(2), .enable("false")) multiplexer_4 (
    .in0(multiplexer_2_out), .in1(2'b10), .out(multiplexer_4_out), .sel(EC2B));
  or or_1 (or_1_out, EC1B, EC1A);
  and and_7 (Stall, or_1_out, EX_MemRd);
  Multiplexer #(.width(2), .enable("false")) multiplexer_5 (
    .in0(multiplexer_3_out), .in1(2'b01), .out(ForwardA), .sel(EC1A));
  Multiplexer #(.width(2), .enable("false")) multiplexer_6 (
    .in0(multiplexer_4_out), .in1(2'b01), .out(ForwardB), .sel(EC1B));

  // Notes on the sheet:
  //   inputs
  //   outputs
endmodule

module PCControl (
  input  JumpR,
  input  Jump,
  input  BEQZ,
  input  BNEZ,
  input  BLTZ,
  input  BGEZ,
  input  BGTZ,
  input  BLEZ,
  input  _0,
  input  _0_2,
  input  _0_3,
  output [1:0] PCSrc,
  output Kill1,
  output Kill2
);

  wire and_2_out, and_3_out, and_4_out, and_5_out, and_6_out, and_7_out, JUMP_t, or_2_out, or_3_out;

  or or_1 (Kill1, Kill2, JUMP_t);
  or or_2 (or_2_out, _0_2, _0);
  or or_3 (or_3_out, _0_2, _0_3);
  or or_4 (PCSrc[0], JumpR, JUMP_t);
  or or_5 (PCSrc[1], JumpR, Kill2);
  and and_1 (JUMP_t, ~Kill2, Jump);  // AND_Gate
  and and_2 (and_2_out, _0_2, BEQZ);
  and and_3 (and_3_out, ~_0_2, BNEZ);  // AND_Gate
  and and_4 (and_4_out, _0_3, BLTZ);
  and and_5 (and_5_out, or_2_out, BGEZ);
  and and_6 (and_6_out, _0, BGTZ);
  and and_7 (and_7_out, or_3_out, BLEZ);
  or or_6 (Kill2, and_2_out, and_3_out, and_4_out, and_5_out, and_6_out, and_7_out);

  // Other names for the same wires on the sheet: BRANCH = Kill2; EQZ = _0_2; GTZ = _0; LTZ = _0_3

  // Notes on the sheet:
  //   PCSrc
  //   KILLs
  //   inputs
  //   BRANCHEs
  //   outputs
endmodule
